// Logisim project ex2-test.circ as structural Verilog: 1 circuit, main circuit main
module main (
  output halt,
  output [1:0] CYCLE,
  output [31:0] INSTRUCTION,
  output BrUn
);

  wire clock_1_out;
  wire [1:0] adder_1_out;

  Comparator #(.width(2)) comparator_1 (.a(2'b11), .b(CYCLE), .eq(halt));  // open: gt, lt
  Register #(.width(2)) register_1 (.D(adder_1_out), .clk(clock_1_out), .Q(CYCLE));  // open: en, clr
  Adder #(.width(2)) adder_1 (.a(CYCLE), .b(2'b01), .out(adder_1_out));  // open: cin, cout
  Clock clock_1 (.out(clock_1_out));
  ROM #(.addrWidth(2), .dataWidth(32)) rom_1 (.addr(CYCLE), .data(INSTRUCTION));
  compute_BrUn compute_brun_1 (.INSTRUCTION(INSTRUCTION), .BrUn(BrUn));

  // Notes on the sheet:
  //   contents of rom_1 (hex, n*v repeats v):
  //   56544063 65645063 56546063 56547063
endmodule
